# Fritzing sketch Fritzing Sketch (saved by Fritzing 1.0.2b)
breadboards: 1

parts:
  Adafruit#1 = Adafruit DRV2605L Haptic Motor Controller - STEMMA QT [part_number=2305]
  Part1 = Adafruit ESP32-S3 Reverse TFT Feather [part_number="Adafruit #5691"]
  R1 = Basic Flex Resistor
  R2 = Resistor [tolerance=±5% resistance=220 package="2512 [SMD]"]
  LSM6DSOX1 = Adafruit_LSM6DSOX

nets:
  GND: Adafruit#1.GND, Part1.GND, LSM6DSOX1.GND
  VCC: Adafruit#1.VCC, Part1.VSENSOR, LSM6DSOX1.VCC
  N1: Adafruit#1.SDA, Part1.SDA, LSM6DSOX1.SDA
  N2: Adafruit#1.SCL, Part1.SCL, LSM6DSOX1.SCL
  N3: Part1.A0, R2.Pin_0
  N4: Part1.3.3V, R1.Pin_1
  N5: R1.Pin_2, R2.Pin_1

custom parts:
  Adafruit DRV2605L Haptic Motor Controller - STEMMA QT: The DRV2605 from TI is a fancy little motor driver. Rather than controlling a stepper motor or DC motor, its designed specifically for controlling haptic motors - buzzers and vibration motors. Normally one would just turn those kinds of motors on and off, but this driver has the ability to have various effects when driving a vibe motor. For example, ramping the vibration level up and down,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
